# Fritzing sketch midithru4 (saved by Fritzing 0.9.3b)
circuit board: 10.0014cm x 5.58884cm
breadboards: 1

parts:
  U1 = MIDI_CONN_FEMALE [package=din_5_female]
  U2 = MIDI_CONN_FEMALE [package=din_5_female]
  U3 = MIDI_CONN_FEMALE [package=din_5_female]
  U4 = MIDI_CONN_FEMALE [package=din_5_female]
  MIDI_IN = MIDI_CONN_FEMALE [package=din_5_female]
  D1 = Rectifier Diode [part_number=1N4001 package="300 mil [THT]"]
  R1 = Resistor [tolerance=±5% resistance=220 package=THT]
  R2 = Resistor [tolerance=±5% resistance=220 package=THT]
  R3 = Resistor [tolerance=±5% resistance=220 package=THT]
  R4 = Resistor [tolerance=±5% resistance=220 package=THT]
  R5 = Resistor [tolerance=±5% resistance=220 package=THT]
  R6 = Resistor [tolerance=±5% resistance=220 package=THT]
  R7 = Resistor [tolerance=±5% resistance=220 package=THT]
  R8 = Resistor [tolerance=±5% resistance=220 package=THT]
  Power_plug1 = Power plug
  R9 = Resistor [tolerance=±5% resistance=220 package=THT]
  R10 = Resistor [tolerance=±5% resistance=220 package=THT]
  LED1 = LED - 5mm [color="Red (633nm)" package="5 mm [THT]"]
  D2 = Rectifier Diode [part_number=1N4001 package="300 mil [THT]"]
  C1 = Electrolytic Capacitor [capacitance=1µF package="100 mil [THT, electrolytic]"]
  U6 = Single Op-Amp [package="DIP8 [THT]"]
  U6_1 = Single Op-Amp [package="DIP8 [THT]"]  # not connected
  U6_3 = Single Op-Amp [package="DIP8 [THT]"]  # not connected
  U7 = Voltage Regulator - 5V [package="TO220 [THT]"]
  C2 = Electrolytic Capacitor [capacitance=1µF package="100 mil [THT, electrolytic]"]
  IC1 = Hex Inverter Schmitt Trigger SN74HC14 [package="DIP (Dual Inline)"]
  R11 = Resistor [tolerance=±5% resistance=220 package=THT]
  C3 = Ceramic Capacitor [capacitance=100nF package="100 mil [THT, multilayer]"]
  LED2 = LED - 5mm [color="Red (633nm)" package="5 mm [THT]"]
  R12 = Resistor [tolerance=±5% resistance=220 package=THT]

nets:
  GND: U1.NC1, U2.NC1, U3.NC1, U4.NC1, Power_plug1.GND, LED1.cathode, C1.-, U6.connector4, U7.GND, C2.-, IC1.GND, C3.0, LED2.cathode
  N1: U1.MIDI_IN, R8.Pin_0
  N2: U1.MIDI_OUT, R7.Pin_0
  N3: U2.MIDI_IN, R6.Pin_0
  N4: U2.MIDI_OUT, R5.Pin_0
  N5: U3.MIDI_IN, R4.Pin_0
  N6: U3.MIDI_OUT, R3.Pin_0
  N7: U4.MIDI_IN, R2.Pin_0
  N8: U4.MIDI_OUT, R1.Pin_0
  N9: MIDI_IN.MIDI_IN, R10.Pin_0
  N10: MIDI_IN.MIDI_OUT, D1.anode, U6.connector2
  N11: D1.cathode, R10.Pin_1, U6.connector1
  N12: R1.Pin_1, IC1.6Y
  N13: R2.Pin_1, R4.Pin_1, R6.Pin_1, R8.Pin_1
  N14: R3.Pin_1, IC1.5Y
  N15: R5.Pin_1, IC1.4Y
  N16: R7.Pin_1, IC1.3Y
  N17: Power_plug1.VCC, D2.anode
  N18: R9.Pin_0, U6.connector7, U7.output_voltage, C2.+, IC1.VCC, R11.Pin_0, C3.1
  N19: R9.Pin_1, LED1.anode
  N20: D2.cathode, C1.+, U7.input_voltage
  N21: U6.connector5, IC1.1A, R11.Pin_1
  N22: IC1.1Y, IC1.2A, IC1.3A, IC1.4A, IC1.5A, IC1.6A
  N23: IC1.2Y, R12.Pin_1
  N24: LED2.anode, R12.Pin_0

custom parts:
  Power plug: power plug
  Single Op-Amp: The classic single Operational Amplifier (Op-Amp).
  Single Op-Amp: The classic single Operational Amplifier (Op-Amp).
  Single Op-Amp: The classic single Operational Amplifier (Op-Amp).
